// Logisim project 2BitAdder.circ as structural Verilog: 1 circuit, main circuit main
module main (
  input  A1,
  input  A2,
  input  B1,
  input  B2,
  output o_1,
  output o_2,
  output o_3
);

  wire carry_1_out, carry_2_out, carry__A__b_out, sum_2_out;

  xor sum_1 (o_1, B1, A1);
  and carry_1 (carry_1_out, A1, B1);
  xor sum_2 (sum_2_out, B2, A2);
  and carry_2 (carry_2_out, A2, B2);
  xor sum_A__B (o_2, sum_2_out, carry_1_out);
  and carry__A__b (carry__A__b_out, carry_1_out, sum_2_out);
  or or_1 (o_3, carry__A__b_out, carry_2_out);
  _7_Segment_Display u_7_segment_display_1 (.b(o_1), .c(o_1));  // open: g, f, a, e, d, dp
endmodule
