// Logisim project CascadingIncrementer.circ as structural Verilog: 3 circuits, main circuit main
module main (
  input  in_1,
  input  in_2,
  input  in_3,
  input  in_4,
  input  in_5,
  input  in_6,
  input  in_7,
  input  in_8,
  output out_9,
  output out_10,
  output out_11,
  output out_12,
  output out_13,
  output out_14,
  output out_15,
  output out_16,
  output out_17
);

  wire and_2_out, and_3_out, and_4_out, and_5_out, and_6_out, and_7_out;

  // AND_Gate and_1 is placed but not wired
  xor xor_1 (out_10, in_1, in_2);
  and and_2 (and_2_out, in_2, in_1);
  xor xor_2 (out_11, in_3, and_2_out);
  and and_3 (and_3_out, and_2_out, in_3);
  xor xor_3 (out_12, and_3_out, in_4);
  and and_4 (and_4_out, and_3_out, in_4);
  xor xor_4 (out_13, in_5, and_4_out);
  and and_5 (and_5_out, in_5, and_4_out);
  xor xor_5 (out_14, in_6, and_5_out);
  and and_6 (and_6_out, in_6, and_5_out);
  xor xor_6 (out_15, in_7, and_6_out);
  and and_7 (and_7_out, and_6_out, in_7);
  xor xor_7 (out_16, in_8, and_7_out);
  and and_8 (out_17, and_7_out, in_8);
  not not_1 (out_9, in_1);
endmodule

module _2 (
  input  a,
  input  b,
  input  c,
  input  d,
  input  e,
  input  f,
  input  g,
  input  h,
  output x,
  output y,
  output z,
  output u,
  output v,
  output w,
  output s,
  output t,
  output x2
);

  wire and_1_out, and_2_out, and_3_out, and_4_out, and_5_out, and_6_out;

  not not_1 (x, a);
  xor xor_1 (y, a, b);
  and and_1 (and_1_out, b, a);
  and and_2 (and_2_out, b, a, c);
  and and_3 (and_3_out, b, a, c, d);
  and and_4 (and_4_out, b, a, c, d, e);
  and and_5 (and_5_out, b, a, c, d, e, f);
  and and_6 (and_6_out, b, a, c, d, e, f, g);
  and and_7 (x2, b, a, c, d, e, f, g, h);
  xor xor_2 (z, c, and_1_out);
  xor xor_3 (u, and_2_out, d);
  xor xor_4 (v, e, and_3_out);
  xor xor_5 (w, f, and_4_out);
  xor xor_6 (s, g, and_5_out);
  xor xor_7 (t, h, and_6_out);
endmodule

module _3 (
  input  a,
  input  b,
  input  c,
  input  d,
  input  e,
  input  f,
  input  g,
  input  h,
  output x,
  output y,
  output z,
  output u,
  output v,
  output w,
  output s,
  output t,
  output x2
);

  wire and_1_out, and_2_out, and_3_out, and_4_out, and_5_out, and_6_out, and_7_out, and_8_out, and_9_out,
       and_10_out, and_11_out, and_12_out, and_13_out, and_14_out, and_15_out, and_16_out, and_17_out,
       and_18_out, and_19_out, and_20_out, and_21_out, and_22_out, and_23_out, and_24_out, and_25_out,
       and_26_out, and_28_out;

  not not_1 (x, a);
  xor xor_1 (y, a, b);
  and and_1 (and_1_out, b, a);
  and and_2 (and_2_out, b, a);
  and and_3 (and_3_out, b, a);
  and and_4 (and_4_out, c, d);
  and and_5 (and_5_out, b, a);
  and and_6 (and_6_out, b, a);
  and and_7 (and_7_out, d, e);
  and and_8 (and_8_out, b, a);
  and and_9 (and_9_out, c, d);
  and and_10 (and_10_out, e, f);
  and and_11 (and_11_out, b, a);
  and and_12 (and_12_out, c, d);
  and and_13 (and_13_out, e, f);
  and and_14 (and_14_out, g, h);
  xor xor_2 (z, c, and_1_out);
  and and_15 (and_15_out, and_2_out, c);
  and and_16 (and_16_out, and_3_out, and_4_out);
  and and_17 (and_17_out, and_5_out, c);
  and and_18 (and_18_out, and_17_out, and_19_out);
  and and_19 (and_19_out, d, e);
  and and_20 (and_20_out, and_6_out, c);
  and and_21 (and_21_out, and_20_out, and_22_out);
  and and_22 (and_22_out, and_7_out, f);
  and and_23 (and_23_out, and_8_out, and_9_out);
  and and_24 (and_24_out, and_23_out, and_25_out);
  and and_25 (and_25_out, and_10_out, g);
  and and_26 (and_26_out, and_11_out, and_12_out);
  and and_27 (x2, and_26_out, and_28_out);
  and and_28 (and_28_out, and_13_out, and_14_out);
  xor xor_3 (u, and_15_out, d);
  xor xor_4 (v, e, and_16_out);
  xor xor_5 (w, f, and_18_out);
  xor xor_6 (s, g, and_21_out);
  xor xor_7 (t, h, and_24_out);
endmodule
