// Logisim project Memory_FF.circ as structural Verilog: 1 circuit, main circuit main
module main (
  input  Clock,
  input  Data,
  input  in_3,
  input  [1:0] in_4,
  output Q,
  output [1:0] out_6
);

  wire and_1_out, and_2_out, and_3_out, and_4_out, nor_1_out, nor_2_out, nor_3_out, not_1_out, not_2_out,
       not_3_out;

  not not_1 (not_1_out, Clock);
  not not_2 (not_2_out, Data);
  not not_3 (not_3_out, nor_2_out);
  Register #(.width(2)) register_1 (.D(in_4), .Q(out_6), .clk(in_3));  // open: en, clr
  and and_1 (and_1_out, not_1_out, Data);
  and and_2 (and_2_out, not_1_out, not_2_out);
  and and_3 (and_3_out, Clock, nor_2_out);
  and and_4 (and_4_out, Clock, not_3_out);
  D_Flip_Flop d_ff_1 (.clk(in_3), .D(in_4[0]));  // open: Q, Qn, preset, en, reset
  D_Flip_Flop d_ff_2 (.clk(in_3), .D(in_4[1]));  // open: Q, Qn, preset, en, reset
  nor nor_1 (nor_1_out, and_1_out, nor_2_out);
  nor nor_2 (nor_2_out, nor_1_out, and_2_out);
  nor nor_3 (nor_3_out, and_3_out, Q);
  nor nor_4 (Q, nor_3_out, and_4_out);
endmodule
