// Logisim project miniac.circ as structural Verilog: 3 circuits, main circuit main
module main (
);

  wire Brancher_selector, Clock_out, RAM_Helper_ld, RAM_Helper_strset, Reset_out;
  wire [7:0] AC_q, adder_1_out, bit_extender_1_out, Brancher_new_pc, multiplexer_1_out, multiplexer_2_out,
       PC_q, ram_1_data, RAM_Helper_to_ac, rom_1_data, shifter_1_out;

  Clock Clock (.out(Clock_out));
  Button Reset (.out(Reset_out));
  Register PC (.D(multiplexer_1_out), .Q(PC_q), .clk(Clock_out), .clr(Reset_out));  // open: en
  Multiplexer #(.width(8)) multiplexer_1 (
    .in0(adder_1_out), .in1(Brancher_new_pc), .out(multiplexer_1_out), .sel(Brancher_selector));  // open: en
  Register AC (.D(multiplexer_2_out), .Q(AC_q), .clk(Clock_out), .clr(Reset_out));  // open: en
  Adder adder_1 (.a(PC_q), .b(8'h1), .out(adder_1_out));  // open: cin, cout
  // Probe on rom_1_data
  ROM rom_1 (.addr(PC_q), .data(rom_1_data));  // open: sel
  Brancher Brancher (
    .Opcode(rom_1_data[7:5]), .AC(AC_q), .PC(PC_q), .Argument(rom_1_data[4:0]), .Selector(Brancher_selector),
    .New_PC(Brancher_new_pc));
  Multiplexer #(.select(3), .width(8)) multiplexer_2 (
    .in3(shifter_1_out), .in4(bit_extender_1_out), .in5(RAM_Helper_to_ac), .in6(RAM_Helper_to_ac),
    .in7(RAM_Helper_to_ac), .out(multiplexer_2_out), .sel(rom_1_data[7:5]));  // open: in0, in1, in2, en
  Shifter #(.shift("rl")) shifter_1 (.in(AC_q), .\dist (rom_1_data[2:0]), .out(shifter_1_out));
  assign bit_extender_1_out = {{3{rom_1_data[4]}}, rom_1_data[4:0]};  // Bit_Extender bit_extender_1
  RAM_helper RAM_Helper (
    .Opcode(rom_1_data[7:5]), .AC_in(AC_q), .To_AC(RAM_Helper_to_ac), .STRSET(RAM_Helper_strset),
    .LD(RAM_Helper_ld), .RAM_in(ram_1_data));
  RAM #(.addrWidth(5), .bus("separate")) ram_1 (
    .addr(rom_1_data[4:0]), .din(AC_q), .data(ram_1_data), .str(RAM_Helper_strset), .clk(Clock_out),
    .ld(RAM_Helper_ld), .clr(Reset_out));  // open: sel

  // Notes on the sheet:
  //   Joseph Benton
  //   CSCI 230 Assn 8
  //   contents of rom_1 (hex, n*v repeats v):
  //   87 41 85 42 80 40 88 43 9f 44 a2 67 42 2a a1 c1 41 9f c3 43 8 80 14 a0 c1 40 80 13 80
  //   argument
  //   op
endmodule

module Brancher (
  input  [2:0] Opcode,
  input  [7:0] AC,
  input  [7:0] PC,
  input  [4:0] Argument,
  output Selector,
  output [7:0] New_PC
);

  wire multiplexer_1_out, nor_1_out, nor_2_out;
  wire [4:0] negator_1_out;
  wire [7:0] adder_1_out, bit_extender_1_out, bit_extender_2_out, subtractor_1_out;

  nor nor_1 (nor_1_out, Opcode[1], Opcode[2]);
  nor nor_2 (nor_2_out, AC[0], AC[1], AC[2], AC[3], AC[4], AC[5], AC[6], AC[7]);
  Negator #(.width(5)) negator_1 (.in(Argument), .out(negator_1_out));
  Multiplexer multiplexer_1 (.in0(nor_2_out), .in1(AC[7]), .out(multiplexer_1_out), .sel(Opcode[0]));  // open: en
  assign bit_extender_1_out = {{3{Argument[4]}}, Argument};  // Bit_Extender bit_extender_1
  assign bit_extender_2_out = {{3{negator_1_out[4]}}, negator_1_out};  // Bit_Extender bit_extender_2
  and and_1 (Selector, nor_1_out, multiplexer_1_out);
  Adder adder_1 (.a(PC), .b(bit_extender_1_out), .out(adder_1_out));  // open: cin, cout
  Subtractor subtractor_1 (.a(PC), .b(bit_extender_2_out), .out(subtractor_1_out));  // open: bin, bout
  Multiplexer #(.width(8)) multiplexer_2 (
    .in0(adder_1_out), .in1(subtractor_1_out), .out(New_PC), .sel(Argument[4]));  // open: en
endmodule

module RAM_helper (
  input  [2:0] Opcode,
  input  [7:0] RAM_in,
  input  [7:0] AC_in,
  output STRSET,
  output LD,
  output [7:0] To_AC
);

  wire and_2_out, and_3_out, and_4_out, not_1_out, not_2_out, not_3_out, not_4_out;
  wire [7:0] adder_1_out, subtractor_1_out;

  not not_1 (not_1_out, Opcode[0]);
  not not_2 (not_2_out, Opcode[2]);
  not not_3 (not_3_out, Opcode[1]);
  not not_4 (not_4_out, Opcode[0]);
  Adder adder_1 (.a(RAM_in), .b(AC_in), .out(adder_1_out));  // open: cin, cout
  Subtractor subtractor_1 (.a(AC_in), .b(RAM_in), .out(subtractor_1_out));  // open: bin, bout
  and and_1 (STRSET, not_1_out, Opcode[1], not_2_out);
  and and_2 (and_2_out, Opcode[2], not_3_out, Opcode[0]);
  and and_3 (and_3_out, Opcode[2], Opcode[1], not_4_out);
  and and_4 (and_4_out, Opcode[2], Opcode[1], Opcode[0]);
  or or_1 (LD, and_2_out, and_3_out, and_4_out);
  Multiplexer #(.select(3), .width(8)) multiplexer_1 (
    .in5(RAM_in), .in6(adder_1_out), .in7(subtractor_1_out), .out(To_AC), .sel(Opcode));  // open: in0, in1, in2, in3, in4, en
endmodule
