// Logisim project shallow-inc (1).circ as structural Verilog: 1 circuit, main circuit main
module main (
  input  a0,
  input  a1,
  input  a2,
  input  a3,
  input  a4,
  input  a5,
  input  a6,
  input  a7,
  output o0,
  output o1,
  output o2,
  output o3,
  output o4,
  output o5,
  output o6,
  output o7,
  output o8
);

  wire and_1_out, and_2_out, and_3_out, and_4_out, and_5_out, and_6_out, and_7_out, and_8_out, and_9_out,
       and_10_out;

  and and_1 (and_1_out, a0, a1);
  and and_2 (and_2_out, a2, a3);
  and and_3 (and_3_out, a4, a5);
  and and_4 (and_4_out, a6, a7);
  and and_5 (and_5_out, and_1_out, and_2_out);
  and and_6 (and_6_out, and_3_out, and_4_out);
  xor xor_1 (o1, a0, a1);
  and and_7 (and_7_out, a2, and_1_out, and_1_out);
  and and_8 (and_8_out, a4, and_5_out);
  xor xor_2 (o2, and_1_out, a2);
  and and_9 (and_9_out, a5, and_8_out);
  xor xor_3 (o3, and_7_out, a3);
  xor xor_4 (o4, and_5_out, a4);
  and and_10 (and_10_out, and_9_out, a7);
  xor xor_5 (o6, a6, and_9_out);
  xor xor_6 (o7, a7, and_10_out);
  xor xor_7 (o5, a5, and_8_out);
  and and_11 (o8, and_5_out, and_6_out);
  not not_1 (o0, a0);

  // Notes on the sheet:
  //   Place your name(s) here.
  //   CSCI 230 Assn 6
endmodule
