// Logisim project summer.circ as structural Verilog: 2 circuits, main circuit main
module main (
);

  wire _0_out, _1_out, _2_out, _3_out, _4_out, _5_out, _6_out, _7_out, _8_out, _9_out, button_out, C_out,
       d_ff_1_q, keypad_1_isclear, keypad_1_isdigit, keypad_1_isplus, keypad_1_press;
  wire [3:0] keypad_1_digit;
  wire [15:0] adder_1_out, adder_2_out, adder_3_out, multiplexer_1_out, multiplexer_2_out, multiplexer_3_out,
       multiplexer_4_out, register_2_q;
  wire [15:1] register_1_q;
  wire [15:15] register_1_q_2;

  // Probe on multiplexer_4_out
  Button _8 (.out(_8_out));
  Button _7 (.out(_7_out));
  Button _5 (.out(_5_out));
  Button _4 (.out(_4_out));
  Button _1 (.out(_1_out));
  Button _2 (.out(_2_out));
  Button _0 (.out(_0_out));
  Button button (.out(button_out));
  Button _9 (.out(_9_out));
  Button _6 (.out(_6_out));
  keypad keypad_1 (
    .digit0(_0_out), .digit1(_1_out), .digit2(_2_out), .digit3(_3_out), .digit4(_4_out), .digit5(_5_out),
    .digit6(_6_out), .digit7(_7_out), .digit8(_8_out), .digit9(_9_out), .digit(keypad_1_digit),
    .press(keypad_1_press), .opPlus(button_out), .opClear(C_out), .isdigit(keypad_1_isdigit),
    .isclear(keypad_1_isclear), .isplus(keypad_1_isplus));
  Button _3 (.out(_3_out));
  Button C (.out(C_out));
  Adder #(.width(16)) adder_1 (
    .a({register_1_q[13:1], 3'b000}), .b({register_1_q, 1'b0}), .out(adder_1_out));  // open: cin, cout
  Adder #(.width(16)) adder_2 (
    .a({{12{1'b0}}, keypad_1_digit}), .b(adder_1_out), .out(adder_2_out));  // open: cin, cout
  Multiplexer #(.width(16)) multiplexer_1 (
    .in0({16{1'b0}}), .in1(adder_2_out), .out(multiplexer_1_out), .sel(keypad_1_isdigit));  // open: en
  Register #(.width(16)) register_1 (
    .D(multiplexer_1_out), .Q({register_1_q_2[15], register_1_q}), .clk(keypad_1_press));  // open: en, clr
  Multiplexer #(.width(16)) multiplexer_2 (
    .in0({16{1'b0}}), .in1(register_2_q), .out(multiplexer_2_out), .sel(keypad_1_isdigit));  // open: en
  Multiplexer #(.width(16)) multiplexer_3 (
    .in0(multiplexer_2_out), .in1(adder_3_out), .out(multiplexer_3_out), .sel(keypad_1_isplus));  // open: en
  Adder #(.width(16)) adder_3 (
    .a({register_1_q_2[15], register_1_q}), .b(register_2_q), .out(adder_3_out));  // open: cin, cout
  Register #(.width(16)) register_2 (.D(multiplexer_3_out), .Q(register_2_q), .clk(keypad_1_press));  // open: en, clr
  Multiplexer #(.width(16)) multiplexer_4 (
    .in0({register_1_q_2[15], register_1_q}), .in1(register_2_q), .out(multiplexer_4_out), .sel(d_ff_1_q));  // open: en
  D_Flip_Flop d_ff_1 (.clk(keypad_1_press), .D(keypad_1_isplus), .Q(d_ff_1_q));  // open: Qn, preset, en, reset

  // Notes on the sheet:
  //   Joseph Benton & Olivier Kwizera
  //   CSCI 230 Assn 7
endmodule

module keypad (
  input  digit0,
  input  digit1,
  input  digit2,
  input  digit3,
  input  digit4,
  input  digit5,
  input  digit6,
  input  digit7,
  input  digit8,
  input  digit9,
  input  opPlus,
  input  opClear,
  output [3:0] digit,
  output isdigit,
  output isplus,
  output isclear,
  output press
);

  wire buffer_1_out, buffer_2_out, buffer_3_out, buffer_4_out, buffer_5_out, buffer_6_out, buffer_7_out,
       buffer_8_out, buffer_9_out, buffer_10_out, buffer_11_out, buffer_12_out, buffer_13_out, buffer_14_out,
       buffer_15_out, buffer_16_out, buffer_17_out, buffer_18_out, buffer_19_out, buffer_20_out,
       buffer_21_out, buffer_22_out, buffer_23_out, buffer_24_out, buffer_25_out, buffer_26_out,
       buffer_27_out, buffer_28_out, buffer_29_out, buffer_30_out, buffer_31_out, buffer_32_out,
       buffer_33_out, buffer_34_out, buffer_35_out, buffer_36_out, buffer_37_out, buffer_38_out,
       buffer_39_out, buffer_40_out, buffer_41_out, buffer_42_out, buffer_43_out, buffer_44_out,
       buffer_45_out, buffer_46_out, buffer_47_out, buffer_48_out, buffer_49_out, buffer_50_out,
       buffer_51_out, buffer_52_out, buffer_53_out, buffer_54_out, buffer_55_out, buffer_56_out,
       buffer_57_out, buffer_58_out, buffer_59_out, buffer_60_out, buffer_61_out, buffer_62_out,
       buffer_63_out, buffer_64_out, buffer_65_out, buffer_66_out, buffer_67_out, buffer_69_out,
       buffer_70_out, or_6_out;

  or or_1 (digit[0], digit1, digit3, digit5, digit7, digit9);
  or or_2 (digit[1], digit2, digit3, 1'b0, digit6, digit7);
  or or_3 (digit[2], digit4, digit5, 1'b0, digit6, digit7);
  or or_4 (digit[3], digit8, digit9);
  or or_5 (isdigit, digit8, digit9, digit7, digit6, digit5, digit4, digit3, digit2, digit1, digit0);
  buf buffer_1 (buffer_1_out, or_6_out);
  or or_6 (or_6_out, isdigit, opPlus, opClear);
  buf buffer_2 (buffer_2_out, buffer_10_out);
  buf buffer_3 (buffer_3_out, buffer_15_out);
  buf buffer_4 (buffer_4_out, buffer_18_out);
  buf buffer_5 (buffer_5_out, buffer_22_out);
  buf buffer_6 (buffer_6_out, buffer_27_out);
  buf buffer_7 (buffer_7_out, buffer_29_out);
  buf buffer_8 (buffer_8_out, buffer_9_out);
  buf buffer_9 (buffer_9_out, buffer_1_out);
  buf buffer_10 (buffer_10_out, buffer_11_out);
  buf buffer_11 (buffer_11_out, buffer_8_out);
  buf buffer_12 (buffer_12_out, buffer_13_out);
  buf buffer_13 (buffer_13_out, buffer_2_out);
  buf buffer_14 (buffer_14_out, buffer_12_out);
  buf buffer_15 (buffer_15_out, buffer_14_out);
  buf buffer_16 (buffer_16_out, buffer_3_out);
  buf buffer_17 (buffer_17_out, buffer_19_out);
  buf buffer_18 (buffer_18_out, buffer_17_out);
  buf buffer_19 (buffer_19_out, buffer_16_out);
  buf buffer_20 (buffer_20_out, buffer_23_out);
  buf buffer_21 (buffer_21_out, buffer_4_out);
  buf buffer_22 (buffer_22_out, buffer_20_out);
  buf buffer_23 (buffer_23_out, buffer_21_out);
  buf buffer_24 (buffer_24_out, buffer_25_out);
  buf buffer_25 (buffer_25_out, buffer_26_out);
  buf buffer_26 (buffer_26_out, buffer_5_out);
  buf buffer_27 (buffer_27_out, buffer_24_out);
  buf buffer_28 (buffer_28_out, buffer_6_out);
  buf buffer_29 (buffer_29_out, buffer_30_out);
  buf buffer_30 (buffer_30_out, buffer_31_out);
  buf buffer_31 (buffer_31_out, buffer_28_out);
  buf buffer_32 (buffer_32_out, buffer_34_out);
  buf buffer_33 (buffer_33_out, buffer_35_out);
  buf buffer_34 (buffer_34_out, buffer_7_out);
  buf buffer_35 (buffer_35_out, buffer_32_out);
  buf buffer_36 (buffer_36_out, buffer_37_out);
  buf buffer_37 (buffer_37_out, buffer_33_out);
  buf buffer_38 (buffer_38_out, buffer_39_out);
  buf buffer_39 (buffer_39_out, buffer_50_out);
  buf buffer_40 (buffer_40_out, buffer_55_out);
  buf buffer_41 (buffer_41_out, buffer_40_out);
  buf buffer_42 (buffer_42_out, buffer_43_out);
  buf buffer_43 (buffer_43_out, buffer_56_out);
  buf buffer_44 (buffer_44_out, buffer_45_out);
  buf buffer_45 (buffer_45_out, buffer_61_out);
  buf buffer_46 (buffer_46_out, buffer_47_out);
  buf buffer_47 (buffer_47_out, buffer_62_out);
  buf buffer_48 (buffer_48_out, buffer_67_out);
  buf buffer_49 (buffer_49_out, buffer_48_out);
  buf buffer_50 (buffer_50_out, buffer_52_out);
  buf buffer_51 (buffer_51_out, buffer_36_out);
  buf buffer_52 (buffer_52_out, buffer_51_out);
  buf buffer_53 (buffer_53_out, buffer_54_out);
  buf buffer_54 (buffer_54_out, buffer_38_out);
  buf buffer_55 (buffer_55_out, buffer_53_out);
  buf buffer_56 (buffer_56_out, buffer_57_out);
  buf buffer_57 (buffer_57_out, buffer_58_out);
  buf buffer_58 (buffer_58_out, buffer_41_out);
  buf buffer_59 (buffer_59_out, buffer_60_out);
  buf buffer_60 (buffer_60_out, buffer_42_out);
  buf buffer_61 (buffer_61_out, buffer_59_out);
  buf buffer_62 (buffer_62_out, buffer_63_out);
  buf buffer_63 (buffer_63_out, buffer_64_out);
  buf buffer_64 (buffer_64_out, buffer_44_out);
  buf buffer_65 (buffer_65_out, buffer_46_out);
  buf buffer_66 (buffer_66_out, buffer_65_out);
  buf buffer_67 (buffer_67_out, buffer_66_out);
  buf buffer_68 (press, buffer_69_out);
  buf buffer_69 (buffer_69_out, buffer_70_out);
  buf buffer_70 (buffer_70_out, buffer_49_out);

  assign isclear = opClear;
  assign isplus = opPlus;
endmodule
